// Digital circuit ex3.dig as structural Verilog
module ex3 (
  input  [1:0] A,
  input  [1:0] B,
  output Y
);

  wire and_1_out, and_2_out, and_3_out, B0_t, B1_t, xnor_1_out;

  not not_1 (B0_t, B[0]);
  not not_2 (B1_t, B[1]);
  and and_1 (and_1_out, A[1], B1_t);
  xnor xnor_1 (xnor_1_out, A[1], B[1]);
  and and_2 (and_2_out, A[0], B0_t);
  and and_3 (and_3_out, xnor_1_out, and_2_out);
  or or_1 (Y, and_1_out, and_3_out);
endmodule

/* Test case EX3 Test:
A B Y 

 0b00 0b00 0
 0b00 0b01 0
 0b00 0b10 0
 0b00 0b11 0
 0b01 0b00 1
 0b01 0b01 0
 0b01 0b10 0
 0b01 0b11 0
 0b10 0b00 1
 0b10 0b01 1
 0b10 0b10 0
 0b10 0b11 0
 0b11 0b00 1
 0b11 0b01 1
 0b11 0b10 1
 0b11 0b11 0
*/
