// Digital circuit alu.dig as structural Verilog
module alu (
  input  [31:0] A,
  input  [31:0] B,
  input  [3:0] ALUOperation,
  output FlagZ,
  output [31:0] Result
);

  wire add_sub_1_overflow, add_sub_1_sign, is__slt_eq, is__sub_eq, or_1_out;
  wire [0:0] comp_out_ext;
  wire [31:0] add_sub_out, boolean_out;

  Comparator #(.Bits(4)) is__sub (.a(ALUOperation), .b(4'b0110), .eq(is__sub_eq));  // open: gt, lt
  Comparator #(.Bits(4)) is__slt (.a(ALUOperation), .b(4'b0111), .eq(is__slt_eq));  // open: gt, lt
  or or_1 (or_1_out, is__sub_eq, is__slt_eq);
  boolean_unit boolean_unit_1 (.A(A), .B(B), .Bool(ALUOperation[1:0]), .Out(boolean_out));
  add_sub add_sub_1 (
    .B(B), .A(A), .Sub(or_1_out), .Out(add_sub_out), .Overflow(add_sub_1_overflow), .Sign(add_sub_1_sign));
  comparator comparator_1 (.Sign(add_sub_1_sign), .Overflow(add_sub_1_overflow), .Result(comp_out_ext[0]));
  Multiplexer #(.Selector_Bits(2), .Bits(32)) multiplexer_1 (
    .sel(ALUOperation[1:0]), .in_0(boolean_out), .in_1(boolean_out), .in_2(add_sub_out),
    .in_3({{31{1'b0}}, comp_out_ext[0]}), .out(Result));
  Comparator #(.Bits(32)) comparator_2 (.a(Result), .b({32{1'b0}}), .eq(FlagZ));  // open: gt, lt

  // Notes on the sheet:
  //   Control Bits
  //   Inputs
  //   Outputs
endmodule
