// Digital circuit control-unit.dig as structural Verilog
module control_unit (
  input  [6:0] opcode_6_0,
  input  [2:0] funct3_2_0,
  input  [6:0] funct7_6_0,
  output RegWrite,
  output ALUSrc,
  output [1:0] ImmSrc_1_0,
  output [3:0] ALUOperation_3_0
);

  wire add, addi, \and , andi, funct3_add, funct3_addi, funct3_and, funct3_andi, funct3_or, funct3_slt,
       funct3_slti, funct3_sub, funct7_add, funct7_and, funct7_or, funct7_slt, funct7_sub, opcodeI, opcodeR,
       \or , slt, slti, sub;
  wire [2:0] A;

  ROM #(.AddrBits(3), .Bits(8)) rom_1 (.A(A), .sel(1'b1), .D({RegWrite, ALUSrc, ImmSrc_1_0, ALUOperation_3_0}));
  PriorityEncoder #(.Selector_Bits(3)) priorityencoder_1 (
    .in0(add), .in1(sub), .in2(\and ), .in3(\or ), .in4(slt), .in5(addi), .in6(slti), .in7(andi), .num(A));  // open: any
  Comparator #(.Bits(7)) u_OpcodeR (.a(opcode_6_0), .b(7'b0110011), .eq(opcodeR));  // open: gt, lt
  Comparator #(.Bits(3)) funct3Add (.a(funct3_2_0), .b(3'b000), .eq(funct3_add));  // open: gt, lt
  Comparator #(.Bits(7)) funct7Add (.a(funct7_6_0), .b({7{1'b0}}), .eq(funct7_add));  // open: gt, lt
  Comparator #(.Bits(3)) funct3Sub (.a(funct3_2_0), .b(3'b000), .eq(funct3_sub));  // open: gt, lt
  Comparator #(.Bits(7)) funct7Sub (.a(funct7_6_0), .b(7'b0100000), .eq(funct7_sub));  // open: gt, lt
  Comparator #(.Bits(3)) funct3And (.a(funct3_2_0), .b(3'b111), .eq(funct3_and));  // open: gt, lt
  Comparator #(.Bits(7)) funct7And (.a(funct7_6_0), .b({7{1'b0}}), .eq(funct7_and));  // open: gt, lt
  Comparator #(.Bits(3)) funct3Or (.a(funct3_2_0), .b(3'b110), .eq(funct3_or));  // open: gt, lt
  Comparator #(.Bits(7)) funct7Or (.a(funct7_6_0), .b({7{1'b0}}), .eq(funct7_or));  // open: gt, lt
  Comparator #(.Bits(3)) funct3Slt (.a(funct3_2_0), .b(3'b010), .eq(funct3_slt));  // open: gt, lt
  Comparator #(.Bits(7)) funct7Slt (.a(funct7_6_0), .b({7{1'b0}}), .eq(funct7_slt));  // open: gt, lt
  and and_1 (add, opcodeR, funct3_add, funct7_add);
  and and_2 (sub, opcodeR, funct3_sub, funct7_sub);
  and and_3 (\and , opcodeR, funct3_and, funct7_and);
  and and_4 (\or , opcodeR, funct3_or, funct7_or);
  and and_5 (slt, opcodeR, funct3_slt, funct7_slt);
  Comparator #(.Bits(7)) u_OpcodeI (.a(opcode_6_0), .b(7'b0010011), .eq(opcodeI));  // open: gt, lt
  Comparator #(.Bits(3)) funct3Addi (.a(funct3_2_0), .b(3'b000), .eq(funct3_addi));  // open: gt, lt
  Comparator #(.Bits(3)) funct3Slti (.a(funct3_2_0), .b(3'b010), .eq(funct3_slti));  // open: gt, lt
  Comparator #(.Bits(3)) funct3Andi (.a(funct3_2_0), .b(3'b111), .eq(funct3_andi));  // open: gt, lt
  and and_6 (addi, opcodeI, funct3_addi);
  and and_7 (slti, opcodeI, funct3_slti);
  and and_8 (andi, opcodeI, funct3_andi);

  // Other names for the same wires on the sheet: ALUOp[3:0] = ALUOperation_3_0;
  //   D_7_0[7:0] = {RegWrite, ALUSrc, ImmSrc_1_0, ALUOperation_3_0}; ImmSrc[1:0] = ImmSrc_1_0;
  //   funct3[2:0] = funct3_2_0; funct7[6:0] = funct7_6_0; opcode[6:0] = opcode_6_0

  // Notes on the sheet:
  //   contents of rom_1 (hex, n*v repeats v):
  //   82,86,80,81,87,c2,c7,c0
endmodule
