// Digital circuit regfile.dig as structural Verilog
module regfile (
  input  [4:0] ReadReg1,
  input  [4:0] ReadReg2,
  input  [4:0] WriteReg,
  input  [31:0] WriteData,
  input  RegWrite,
  input  Clock,
  output [31:0] ReadData1,
  output [31:0] ReadData2
);

  wire and_1_out, and_2_out, and_3_out, and_4_out, and_5_out, and_6_out, and_7_out, and_8_out, and_9_out,
       and_10_out, and_11_out, and_12_out, and_13_out, and_14_out, and_15_out, and_16_out, and_17_out,
       and_18_out, and_19_out, and_20_out, and_21_out, and_22_out, and_23_out, and_24_out, and_25_out,
       and_26_out, and_27_out, and_28_out, and_29_out, and_30_out, and_31_out, Dec0, Dec1, Dec2, Dec3, Dec4,
       Dec5, Dec6, Dec7, Dec8, Dec9, Dec10, Dec11, Dec12, Dec13, Dec14, Dec15, Dec16, Dec17, Dec18, Dec19,
       Dec20, Dec21, Dec22, Dec23, Dec24, Dec25, Dec26, Dec27, Dec28, Dec29, Dec30, Dec31;
  wire [31:0] R0, R1, R2, R3, R4, R5, R6, R7, R8, R9, R10, R11, R12, R13, R14, R15, R16, R17, R18, R19, R20,
       R21, R22, R23, R24, R25, R26, R27, R28, R29, R30, R31;

  and and_1 (and_1_out, RegWrite, Dec8);
  and and_2 (and_2_out, RegWrite, Dec16);
  and and_3 (and_3_out, RegWrite, Dec24);
  Register #(.Bits(32)) u_R0 (.D(WriteData), .C(Clock), .en(1'b0), .Q(R0));
  Register #(.Bits(32)) u_R8 (.D(WriteData), .C(Clock), .en(and_1_out), .Q(R8));
  Register #(.Bits(32)) u_R16 (.D(WriteData), .C(Clock), .en(and_2_out), .Q(R16));
  Register #(.Bits(32)) u_R24 (.D(WriteData), .C(Clock), .en(and_3_out), .Q(R24));
  and and_4 (and_4_out, RegWrite, Dec1);
  and and_5 (and_5_out, RegWrite, Dec9);
  and and_6 (and_6_out, RegWrite, Dec17);
  and and_7 (and_7_out, RegWrite, Dec25);
  Register #(.Bits(32)) u_R1 (.D(WriteData), .C(Clock), .en(and_4_out), .Q(R1));
  Register #(.Bits(32)) u_R9 (.D(WriteData), .C(Clock), .en(and_5_out), .Q(R9));
  Register #(.Bits(32)) u_R17 (.D(WriteData), .C(Clock), .en(and_6_out), .Q(R17));
  Register #(.Bits(32)) u_R25 (.D(WriteData), .C(Clock), .en(and_7_out), .Q(R25));
  and and_8 (and_8_out, RegWrite, Dec2);
  and and_9 (and_9_out, RegWrite, Dec10);
  and and_10 (and_10_out, RegWrite, Dec18);
  and and_11 (and_11_out, RegWrite, Dec26);
  Register #(.Bits(32)) u_R2 (.D(WriteData), .C(Clock), .en(and_8_out), .Q(R2));
  Register #(.Bits(32)) u_R10 (.D(WriteData), .C(Clock), .en(and_9_out), .Q(R10));
  Register #(.Bits(32)) u_R18 (.D(WriteData), .C(Clock), .en(and_10_out), .Q(R18));
  Register #(.Bits(32)) u_R26 (.D(WriteData), .C(Clock), .en(and_11_out), .Q(R26));
  and and_12 (and_12_out, RegWrite, Dec3);
  and and_13 (and_13_out, RegWrite, Dec11);
  and and_14 (and_14_out, RegWrite, Dec19);
  and and_15 (and_15_out, RegWrite, Dec27);
  Register #(.Bits(32)) u_R3 (.D(WriteData), .C(Clock), .en(and_12_out), .Q(R3));
  Register #(.Bits(32)) u_R11 (.D(WriteData), .C(Clock), .en(and_13_out), .Q(R11));
  Register #(.Bits(32)) u_R19 (.D(WriteData), .C(Clock), .en(and_14_out), .Q(R19));
  Register #(.Bits(32)) u_R27 (.D(WriteData), .C(Clock), .en(and_15_out), .Q(R27));
  and and_16 (and_16_out, RegWrite, Dec4);
  and and_17 (and_17_out, RegWrite, Dec12);
  and and_18 (and_18_out, RegWrite, Dec20);
  and and_19 (and_19_out, RegWrite, Dec28);
  Register #(.Bits(32)) u_R4 (.D(WriteData), .C(Clock), .en(and_16_out), .Q(R4));
  Register #(.Bits(32)) u_R12 (.D(WriteData), .C(Clock), .en(and_17_out), .Q(R12));
  Register #(.Bits(32)) u_R20 (.D(WriteData), .C(Clock), .en(and_18_out), .Q(R20));
  Register #(.Bits(32)) u_R28 (.D(WriteData), .C(Clock), .en(and_19_out), .Q(R28));
  Multiplexer #(.Selector_Bits(5), .Bits(32)) multiplexer_1 (
    .sel(ReadReg1), .in_0(R0), .in_1(R1), .in_2(R2), .in_3(R3), .in_4(R4), .in_5(R5), .in_6(R6), .in_7(R7),
    .in_8(R8), .in_9(R9), .in_10(R10), .in_11(R11), .in_12(R12), .in_13(R13), .in_14(R14), .in_15(R15),
    .in_16(R16), .in_17(R17), .in_18(R18), .in_19(R19), .in_20(R20), .in_21(R21), .in_22(R22), .in_23(R23),
    .in_24(R24), .in_25(R25), .in_26(R26), .in_27(R27), .in_28(R28), .in_29(R29), .in_30(R30), .in_31(R31),
    .out(ReadData1));
  and and_20 (and_20_out, RegWrite, Dec5);
  and and_21 (and_21_out, RegWrite, Dec13);
  and and_22 (and_22_out, RegWrite, Dec21);
  and and_23 (and_23_out, RegWrite, Dec29);
  Register #(.Bits(32)) u_R5 (.D(WriteData), .C(Clock), .en(and_20_out), .Q(R5));
  Register #(.Bits(32)) u_R13 (.D(WriteData), .C(Clock), .en(and_21_out), .Q(R13));
  Register #(.Bits(32)) u_R21 (.D(WriteData), .C(Clock), .en(and_22_out), .Q(R21));
  Register #(.Bits(32)) u_R29 (.D(WriteData), .C(Clock), .en(and_23_out), .Q(R29));
  Multiplexer #(.Selector_Bits(5), .Bits(32)) multiplexer_2 (
    .sel(ReadReg2), .in_0(R0), .in_1(R1), .in_2(R2), .in_3(R3), .in_4(R4), .in_5(R5), .in_6(R6), .in_7(R7),
    .in_8(R8), .in_9(R9), .in_10(R10), .in_11(R11), .in_12(R12), .in_13(R13), .in_14(R14), .in_15(R15),
    .in_16(R16), .in_17(R17), .in_18(R18), .in_19(R19), .in_20(R20), .in_21(R21), .in_22(R22), .in_23(R23),
    .in_24(R24), .in_25(R25), .in_26(R26), .in_27(R27), .in_28(R28), .in_29(R29), .in_30(R30), .in_31(R31),
    .out(ReadData2));
  and and_24 (and_24_out, RegWrite, Dec6);
  and and_25 (and_25_out, RegWrite, Dec14);
  and and_26 (and_26_out, RegWrite, Dec22);
  and and_27 (and_27_out, RegWrite, Dec30);
  Register #(.Bits(32)) u_R6 (.D(WriteData), .C(Clock), .en(and_24_out), .Q(R6));
  Register #(.Bits(32)) u_R14 (.D(WriteData), .C(Clock), .en(and_25_out), .Q(R14));
  Register #(.Bits(32)) u_R22 (.D(WriteData), .C(Clock), .en(and_26_out), .Q(R22));
  Register #(.Bits(32)) u_R30 (.D(WriteData), .C(Clock), .en(and_27_out), .Q(R30));
  Decoder #(.Selector_Bits(5)) decoder_1 (
    .sel(WriteReg), .out_0(Dec0), .out_1(Dec1), .out_2(Dec2), .out_3(Dec3), .out_4(Dec4), .out_5(Dec5),
    .out_6(Dec6), .out_7(Dec7), .out_8(Dec8), .out_9(Dec9), .out_10(Dec10), .out_11(Dec11), .out_12(Dec12),
    .out_13(Dec13), .out_14(Dec14), .out_15(Dec15), .out_16(Dec16), .out_17(Dec17), .out_18(Dec18),
    .out_19(Dec19), .out_20(Dec20), .out_21(Dec21), .out_22(Dec22), .out_23(Dec23), .out_24(Dec24),
    .out_25(Dec25), .out_26(Dec26), .out_27(Dec27), .out_28(Dec28), .out_29(Dec29), .out_30(Dec30),
    .out_31(Dec31));
  and and_28 (and_28_out, RegWrite, Dec7);
  and and_29 (and_29_out, RegWrite, Dec15);
  and and_30 (and_30_out, RegWrite, Dec23);
  and and_31 (and_31_out, RegWrite, Dec31);
  Register #(.Bits(32)) u_R7 (.D(WriteData), .C(Clock), .en(and_28_out), .Q(R7));
  Register #(.Bits(32)) u_R15 (.D(WriteData), .C(Clock), .en(and_29_out), .Q(R15));
  Register #(.Bits(32)) u_R23 (.D(WriteData), .C(Clock), .en(and_30_out), .Q(R23));
  Register #(.Bits(32)) u_R31 (.D(WriteData), .C(Clock), .en(and_31_out), .Q(R31));
endmodule
